// Logisim project part2a.circ as structural Verilog: 2 circuits, main circuit register_file
module register_file (
  input  CLK,
  input  [1:0] FunSel,
  input  [7:0] I,
  input  [3:0] RegSel,
  input  [3:0] TmpSel,
  input  [2:0] OutASel,
  input  [2:0] OutBSel,
  output [7:0] OutA,
  output [7:0] OutB
);

  wire [3:0] not_1_out, not_2_out;
  wire [7:0] R1_output, R2_output, R3_output, R4_output, T1_output, T2_output, T3_output, T4_output;

  Hex_Digit_Display hex_digit_display_1 (.value(I[3:0]));  // open: dp
  Hex_Digit_Display hex_digit_display_2 (.value(I[7:4]));  // open: dp
  assign not_1_out = ~RegSel;  // NOT_Gate not_1, 4 bits wide
  _8_bit_register R1 (.INPUT(I), .CLK(CLK), .ENABLE(not_1_out[3]), .FUNSEL(FunSel), .OUTPUT(R1_output));
  _8_bit_register R2 (.INPUT(I), .CLK(CLK), .ENABLE(not_1_out[2]), .FUNSEL(FunSel), .OUTPUT(R2_output));
  _8_bit_register R3 (.INPUT(I), .CLK(CLK), .ENABLE(not_1_out[1]), .FUNSEL(FunSel), .OUTPUT(R3_output));
  _8_bit_register R4 (.INPUT(I), .CLK(CLK), .ENABLE(not_1_out[0]), .FUNSEL(FunSel), .OUTPUT(R4_output));
  assign not_2_out = ~TmpSel;  // NOT_Gate not_2, 4 bits wide
  _8_bit_register T1 (.INPUT(I), .CLK(CLK), .ENABLE(not_2_out[3]), .FUNSEL(FunSel), .OUTPUT(T1_output));
  _8_bit_register T2 (.INPUT(I), .CLK(CLK), .ENABLE(not_2_out[2]), .FUNSEL(FunSel), .OUTPUT(T2_output));
  _8_bit_register T3 (.INPUT(I), .CLK(CLK), .ENABLE(not_2_out[1]), .FUNSEL(FunSel), .OUTPUT(T3_output));
  _8_bit_register T4 (.INPUT(I), .CLK(CLK), .ENABLE(not_2_out[0]), .FUNSEL(FunSel), .OUTPUT(T4_output));
  Multiplexer #(.select(3), .width(8)) multiplexer_1 (
    .in0(R1_output), .in1(R2_output), .in2(R3_output), .in3(R4_output), .in4(T1_output), .in5(T2_output),
    .in6(T3_output), .in7(T4_output), .out(OutA), .sel(OutASel));  // open: en
  Multiplexer #(.select(3), .width(8)) multiplexer_2 (
    .in0(R1_output), .in1(R2_output), .in2(R3_output), .in3(R4_output), .in4(T1_output), .in5(T2_output),
    .in6(T3_output), .in7(T4_output), .out(OutB), .sel(OutBSel));  // open: en
  Hex_Digit_Display hex_digit_display_3 (.value(OutA[3:0]));  // open: dp
  Hex_Digit_Display hex_digit_display_4 (.value(OutA[7:4]));  // open: dp
  Hex_Digit_Display hex_digit_display_5 (.value(OutB[7:4]));  // open: dp
  Hex_Digit_Display hex_digit_display_6 (.value(OutB[3:0]));  // open: dp
endmodule

module _8_bit_register (
  input  CLK,
  input  ENABLE,
  input  [7:0] INPUT,
  input  [1:0] FUNSEL,
  output [7:0] OUTPUT
);

  wire [7:0] adder_1_out, multiplexer_1_out, subtractor_1_out;

  Hex_Digit_Display hex_digit_display_1 (.value(INPUT[7:4]));  // open: dp
  Hex_Digit_Display hex_digit_display_2 (.value(INPUT[3:0]));  // open: dp
  Subtractor subtractor_1 (.a(OUTPUT), .b(8'h1), .out(subtractor_1_out));  // open: bin, bout
  Adder adder_1 (.a(OUTPUT), .b(8'h1), .out(adder_1_out));  // open: cin, cout
  Multiplexer #(.select(2), .width(8)) multiplexer_1 (
    .in0(subtractor_1_out), .in1(adder_1_out), .in2(INPUT), .in3({8{1'b0}}), .out(multiplexer_1_out),
    .sel(FUNSEL));  // open: en
  Clock clock_1 ();  // open: out
  D_Flip_Flop d_ff_1 (.clk(CLK), .D(multiplexer_1_out[0]), .Q(OUTPUT[0]), .en(ENABLE));  // open: Qn, preset, reset
  D_Flip_Flop d_ff_2 (.clk(CLK), .D(multiplexer_1_out[1]), .Q(OUTPUT[1]), .en(ENABLE));  // open: Qn, preset, reset
  D_Flip_Flop d_ff_3 (.clk(CLK), .D(multiplexer_1_out[2]), .Q(OUTPUT[2]), .en(ENABLE));  // open: Qn, preset, reset
  D_Flip_Flop d_ff_4 (.clk(CLK), .D(multiplexer_1_out[3]), .Q(OUTPUT[3]), .en(ENABLE));  // open: Qn, preset, reset
  D_Flip_Flop d_ff_5 (.clk(CLK), .D(multiplexer_1_out[4]), .Q(OUTPUT[4]), .en(ENABLE));  // open: Qn, preset, reset
  D_Flip_Flop d_ff_6 (.clk(CLK), .D(multiplexer_1_out[5]), .Q(OUTPUT[5]), .en(ENABLE));  // open: Qn, preset, reset
  D_Flip_Flop d_ff_7 (.clk(CLK), .D(multiplexer_1_out[6]), .Q(OUTPUT[6]), .en(ENABLE));  // open: Qn, preset, reset
  D_Flip_Flop d_ff_8 (.clk(CLK), .D(multiplexer_1_out[7]), .Q(OUTPUT[7]), .en(ENABLE));  // open: Qn, preset, reset
  Hex_Digit_Display hex_digit_display_3 (.value(OUTPUT[7:4]));  // open: dp
  Hex_Digit_Display hex_digit_display_4 (.value(OUTPUT[3:0]));  // open: dp

  // Notes on the sheet:
  //   CLEAR
endmodule
