// Logisim project part2b.circ as structural Verilog: 2 circuits, main circuit main
module main (
  input  CLK,
  input  [1:0] FunSel,
  input  [7:0] I,
  input  [1:0] OutCSel,
  input  [2:0] RegSel,
  input  [1:0] OutDSel,
  output [7:0] OutC,
  output [7:0] OutD
);

  wire [2:0] not_1_out;
  wire [7:0] AR_output, PC_output, SP_output;

  Hex_Digit_Display hex_digit_display_1 (.value(I[7:4]));  // open: dp
  Hex_Digit_Display hex_digit_display_2 (.value(I[3:0]));  // open: dp
  assign not_1_out = ~RegSel;  // NOT_Gate not_1, 3 bits wide
  _8_bit_register PC (.INPUT(I), .CLK(CLK), .ENABLE(not_1_out[2]), .FUNSEL(FunSel), .OUTPUT(PC_output));
  _8_bit_register AR (.INPUT(I), .CLK(CLK), .ENABLE(not_1_out[1]), .FUNSEL(FunSel), .OUTPUT(AR_output));
  _8_bit_register SP (.INPUT(I), .CLK(CLK), .ENABLE(not_1_out[0]), .FUNSEL(FunSel), .OUTPUT(SP_output));
  Hex_Digit_Display hex_digit_display_3 (.value(OutC[7:4]));  // open: dp
  Multiplexer #(.select(2), .width(8)) multiplexer_1 (
    .in0(PC_output), .in1(PC_output), .in2(AR_output), .in3(SP_output), .out(OutC), .sel(OutCSel));  // open: en
  Hex_Digit_Display hex_digit_display_4 (.value(OutD[7:4]));  // open: dp
  Multiplexer #(.select(2), .width(8)) multiplexer_2 (
    .in0(PC_output), .in1(PC_output), .in2(AR_output), .in3(SP_output), .out(OutD), .sel(OutDSel));  // open: en
  Hex_Digit_Display hex_digit_display_5 (.value(OutC[3:0]));  // open: dp
  Hex_Digit_Display hex_digit_display_6 (.value(OutD[3:0]));  // open: dp
endmodule

module _8_bit_register (
  input  CLK,
  input  ENABLE,
  input  [7:0] INPUT,
  input  [1:0] FUNSEL,
  output [7:0] OUTPUT
);

  wire [7:0] adder_1_out, multiplexer_1_out, subtractor_1_out;

  Hex_Digit_Display hex_digit_display_1 (.value(INPUT[7:4]));  // open: dp
  Hex_Digit_Display hex_digit_display_2 (.value(INPUT[3:0]));  // open: dp
  Subtractor subtractor_1 (.a(OUTPUT), .b(8'h1), .out(subtractor_1_out));  // open: bin, bout
  Adder adder_1 (.a(OUTPUT), .b(8'h1), .out(adder_1_out));  // open: cin, cout
  Multiplexer #(.select(2), .width(8)) multiplexer_1 (
    .in0(subtractor_1_out), .in1(adder_1_out), .in2(INPUT), .in3({8{1'b0}}), .out(multiplexer_1_out),
    .sel(FUNSEL));  // open: en
  Clock clock_1 ();  // open: out
  D_Flip_Flop d_ff_1 (.clk(CLK), .D(multiplexer_1_out[0]), .Q(OUTPUT[0]), .en(ENABLE));  // open: Qn, preset, reset
  D_Flip_Flop d_ff_2 (.clk(CLK), .D(multiplexer_1_out[1]), .Q(OUTPUT[1]), .en(ENABLE));  // open: Qn, preset, reset
  D_Flip_Flop d_ff_3 (.clk(CLK), .D(multiplexer_1_out[2]), .Q(OUTPUT[2]), .en(ENABLE));  // open: Qn, preset, reset
  D_Flip_Flop d_ff_4 (.clk(CLK), .D(multiplexer_1_out[3]), .Q(OUTPUT[3]), .en(ENABLE));  // open: Qn, preset, reset
  D_Flip_Flop d_ff_5 (.clk(CLK), .D(multiplexer_1_out[4]), .Q(OUTPUT[4]), .en(ENABLE));  // open: Qn, preset, reset
  D_Flip_Flop d_ff_6 (.clk(CLK), .D(multiplexer_1_out[5]), .Q(OUTPUT[5]), .en(ENABLE));  // open: Qn, preset, reset
  D_Flip_Flop d_ff_7 (.clk(CLK), .D(multiplexer_1_out[6]), .Q(OUTPUT[6]), .en(ENABLE));  // open: Qn, preset, reset
  D_Flip_Flop d_ff_8 (.clk(CLK), .D(multiplexer_1_out[7]), .Q(OUTPUT[7]), .en(ENABLE));  // open: Qn, preset, reset
  Hex_Digit_Display hex_digit_display_3 (.value(OUTPUT[7:4]));  // open: dp
  Hex_Digit_Display hex_digit_display_4 (.value(OUTPUT[3:0]));  // open: dp

  // Notes on the sheet:
  //   CLEAR
endmodule
