// Logisim project part3.circ as structural Verilog: 7 circuits, main circuit ALU(part3)
module main (
  input  [7:0] A,
  input  [7:0] B,
  input  [3:0] FunSel,
  output [3:0] ZCNO,
  output [7:0] OutALU
);

  wire clock_1_out;
  wire [3:0] alu_part3_1_zcno;

  Hex_Digit_Display hex_digit_display_1 (.value(A[3:0]));  // open: dp
  Hex_Digit_Display hex_digit_display_2 (.value(A[7:4]));  // open: dp
  Hex_Digit_Display hex_digit_display_3 (.value(B[7:4]));  // open: dp
  Hex_Digit_Display hex_digit_display_4 (.value(B[3:0]));  // open: dp
  Clock clock_1 (.out(clock_1_out));
  ALU_part3 alu_part3_1 (.A(A), .B(B), .FunSel(FunSel), .c_in(ZCNO[2]), .ZCNO(alu_part3_1_zcno), .OutALU(OutALU));
  flag_register flag_register_1 (.ZCNO_in(alu_part3_1_zcno), .CLK(clock_1_out), .ZCNO_out(ZCNO));
  Hex_Digit_Display hex_digit_display_5 (.value(OutALU[7:4]));  // open: dp
  Hex_Digit_Display hex_digit_display_6 (.value(OutALU[3:0]));  // open: dp

  // Notes on the sheet:
  //   flag_register
endmodule

module ALU_part3 (
  input  [7:0] A,
  input  [7:0] B,
  input  [3:0] FunSel,
  input  c_in,
  output [3:0] ZCNO,
  output [7:0] OutALU
);

  wire arithmetic_operations_1_c_out, arithmetic_operations_1_overflow, arithmetic_shift_1_overflow,
       circular_shift_1_cout, decoder_1_out4, decoder_1_out5, decoder_1_out6, decoder_1_out10,
       decoder_1_out11, decoder_1_out12, decoder_1_out13, decoder_1_out14, decoder_1_out15,
       logical_shift_1_carry, multiplexer_2_out, multiplexer_3_out, not_4_out, or_2_out, or_3_out, or_4_out,
       xor_2_out;
  wire [7:0] and_1_out, arithmetic_operations_1_output, arithmetic_shift_1_output, circular_shift_1_output,
       logical_shift_1_output, not_1_out, not_2_out, or_1_out, xor_1_out;

  Hex_Digit_Display hex_digit_display_1 (.value(A[7:4]));  // open: dp
  Hex_Digit_Display hex_digit_display_2 (.value(A[3:0]));  // open: dp
  Hex_Digit_Display hex_digit_display_3 (.value(B[7:4]));  // open: dp
  Hex_Digit_Display hex_digit_display_4 (.value(B[3:0]));  // open: dp
  arithmetic_operations arithmetic_operations_1 (
    .A(A), .B(B), .FunSel(FunSel[1:0]), .c_in(c_in), .OUTPUT(arithmetic_operations_1_output),
    .c_out(arithmetic_operations_1_c_out), .overflow(arithmetic_operations_1_overflow));
  logical_shift logical_shift_1 (
    .L_R(FunSel[0]), .\output (logical_shift_1_output), .\ınput (A), .CARRY(logical_shift_1_carry));
  arithmetic_shift arithmetic_shift_1 (
    .L_R(FunSel[0]), .\output (arithmetic_shift_1_output), .\ınput (A), .overflow(arithmetic_shift_1_overflow));
  circular_shift circular_shift_1 (
    .L_R(FunSel[0]), .Cin(c_in), .Cout(circular_shift_1_cout), .\output (circular_shift_1_output), .\ınput (A));
  assign xor_1_out = A ^ B;  // XOR_Gate xor_1, 8 bits wide
  assign or_1_out = A | B;  // OR_Gate or_1, 8 bits wide
  assign and_1_out = A & B;  // AND_Gate and_1, 8 bits wide
  assign not_1_out = ~B;  // NOT_Gate not_1, 8 bits wide
  assign not_2_out = ~A;  // NOT_Gate not_2, 8 bits wide
  Multiplexer #(.select(4), .width(8)) multiplexer_1 (
    .in0(A), .in1(B), .in2(not_2_out), .in3(not_1_out), .in4(arithmetic_operations_1_output),
    .in5(arithmetic_operations_1_output), .in6(arithmetic_operations_1_output), .in7(and_1_out),
    .in8(or_1_out), .in9(xor_1_out), .in10(logical_shift_1_output), .in11(logical_shift_1_output),
    .in12(arithmetic_shift_1_output), .in13(arithmetic_shift_1_output), .in14(circular_shift_1_output),
    .in15(circular_shift_1_output), .out(OutALU), .sel(FunSel));  // open: en
  Multiplexer #(.select(2), .enable("false")) multiplexer_2 (
    .in0(arithmetic_operations_1_c_out), .in1(arithmetic_operations_1_c_out), .in2(logical_shift_1_carry),
    .in3(circular_shift_1_cout), .out(multiplexer_2_out), .sel(FunSel[3:2]));
  Multiplexer #(.select(3), .enable("false")) multiplexer_3 (
    .in0(1'b1), .in1(1'b1), .in2(arithmetic_operations_1_overflow), .in3(arithmetic_operations_1_overflow),
    .in4(1'b1), .in5(1'b1), .in6(arithmetic_shift_1_overflow), .out(multiplexer_3_out), .sel(FunSel[3:1]));  // open: in7
  or or_2 (or_2_out, OutALU[0], OutALU[1], OutALU[2], OutALU[3], OutALU[4], OutALU[5], OutALU[6], OutALU[7]);
  xor xor_2 (xor_2_out, OutALU[7], 1'b0);
  Hex_Digit_Display hex_digit_display_5 (.value(OutALU[3:0]));  // open: dp
  Hex_Digit_Display hex_digit_display_6 (.value(OutALU[7:4]));  // open: dp
  not not_3 (ZCNO[3], or_2_out);
  Decoder #(.select(4), .enable("false")) decoder_1 (
    .out4(decoder_1_out4), .out5(decoder_1_out5), .out6(decoder_1_out6), .out10(decoder_1_out10),
    .out11(decoder_1_out11), .out12(decoder_1_out12), .out13(decoder_1_out13), .out14(decoder_1_out14),
    .out15(decoder_1_out15), .sel(FunSel));  // open: out0, out1, out2, out3, out7, out8, out9
  or or_3 (or_3_out, decoder_1_out4, decoder_1_out5, decoder_1_out6, decoder_1_out10, decoder_1_out14, decoder_1_out15, decoder_1_out11);
  not not_4 (not_4_out, decoder_1_out13);
  assign ZCNO[2] = or_3_out ? multiplexer_2_out : 1'bz;  // Controlled_Buffer controlled_buffer_1
  assign ZCNO[1] = not_4_out ? xor_2_out : 1'bz;  // Controlled_Buffer controlled_buffer_2
  or or_4 (or_4_out, decoder_1_out4, decoder_1_out5, decoder_1_out6, decoder_1_out12);
  assign ZCNO[0] = or_4_out ? multiplexer_3_out : 1'bz;  // Controlled_Buffer controlled_buffer_3

  // Notes on the sheet:
  //   c_out
  //   overflow
endmodule

module arithmetic_operations (
  input  [7:0] A,
  input  [7:0] B,
  input  [1:0] FunSel,
  input  c_in,
  output [7:0] OUTPUT,
  output c_out,
  output overflow
);

  wire and_1_out, and_2_out, multiplexer_2_out, not_1_out, not_3_out, not_4_out, xor_1_out;
  wire [7:0] multiplexer_1_out, not_2_out;

  not not_1 (not_1_out, A[7]);
  Multiplexer #(.width(8), .enable("false")) multiplexer_1 (
    .in0(B), .in1(not_2_out), .out(multiplexer_1_out), .sel(FunSel[1]));
  assign not_2_out = ~B;  // NOT_Gate not_2, 8 bits wide
  Multiplexer #(.select(2), .enable("false")) multiplexer_2 (
    .in0(1'b0), .in1(c_in), .in2(1'b1), .out(multiplexer_2_out), .sel(FunSel));  // open: in3
  Adder adder_1 (.a(A), .b(multiplexer_1_out), .out(OUTPUT), .cin(multiplexer_2_out), .cout(c_out));
  xor xor_1 (xor_1_out, multiplexer_2_out, B[7]);
  not not_3 (not_3_out, xor_1_out);
  not not_4 (not_4_out, OUTPUT[7]);
  and and_1 (and_1_out, OUTPUT[7], not_3_out, not_1_out);
  or or_1 (overflow, and_1_out, and_2_out);
  and and_2 (and_2_out, not_4_out, xor_1_out, A[7]);
endmodule

module circular_shift (
  input  L_R,
  input  Cin,
  input  [7:0] \ınput ,
  output [7:0] \output ,
  output Cout
);

  Multiplexer #(.enable("false")) multiplexer_1 (.in0(\ınput [6]), .in1(Cin), .out(\output [7]), .sel(L_R));
  Multiplexer #(.enable("false")) multiplexer_2 (.in0(\ınput [5]), .in1(\ınput [7]), .out(\output [6]), .sel(L_R));
  Multiplexer #(.enable("false")) multiplexer_3 (.in0(\ınput [7]), .in1(\ınput [0]), .out(Cout), .sel(L_R));
  Multiplexer #(.enable("false")) multiplexer_4 (.in0(\ınput [4]), .in1(\ınput [6]), .out(\output [5]), .sel(L_R));
  Multiplexer #(.enable("false")) multiplexer_5 (.in0(\ınput [3]), .in1(\ınput [5]), .out(\output [4]), .sel(L_R));
  Multiplexer #(.enable("false")) multiplexer_6 (.in0(\ınput [2]), .in1(\ınput [4]), .out(\output [3]), .sel(L_R));
  Multiplexer #(.enable("false")) multiplexer_7 (.in0(\ınput [1]), .in1(\ınput [3]), .out(\output [2]), .sel(L_R));
  Multiplexer #(.enable("false")) multiplexer_8 (.in0(\ınput [0]), .in1(\ınput [2]), .out(\output [1]), .sel(L_R));
  Multiplexer #(.enable("false")) multiplexer_9 (.in0(Cin), .in1(\ınput [1]), .out(\output [0]), .sel(L_R));
endmodule

module logical_shift (
  input  L_R,
  input  [7:0] \ınput ,
  output [7:0] \output ,
  output CARRY
);

  Multiplexer #(.enable("false")) multiplexer_1 (.in0(\ınput [6]), .in1(1'b0), .out(\output [7]), .sel(L_R));
  Multiplexer #(.enable("false")) multiplexer_2 (.in0(\ınput [5]), .in1(\ınput [7]), .out(\output [6]), .sel(L_R));
  Multiplexer #(.enable("false")) multiplexer_3 (.in0(\ınput [4]), .in1(\ınput [6]), .out(\output [5]), .sel(L_R));
  Multiplexer #(.enable("false")) multiplexer_4 (.in0(\ınput [3]), .in1(\ınput [5]), .out(\output [4]), .sel(L_R));
  Multiplexer #(.enable("false")) multiplexer_5 (.in0(\ınput [2]), .in1(\ınput [4]), .out(\output [3]), .sel(L_R));
  Multiplexer #(.enable("false")) multiplexer_6 (.in0(\ınput [1]), .in1(\ınput [3]), .out(\output [2]), .sel(L_R));
  Multiplexer #(.enable("false")) multiplexer_7 (.in0(\ınput [0]), .in1(\ınput [2]), .out(\output [1]), .sel(L_R));
  Multiplexer #(.enable("false")) multiplexer_8 (.in0(1'b0), .in1(\ınput [1]), .out(\output [0]), .sel(L_R));
  Multiplexer #(.enable("false")) multiplexer_9 (.in0(\ınput [7]), .in1(\ınput [0]), .out(CARRY), .sel(1'b0));
endmodule

module arithmetic_shift (
  input  L_R,
  input  [7:0] \ınput ,
  output [7:0] \output ,
  output overflow
);

  Multiplexer #(.enable("false")) multiplexer_1 (.in0(\ınput [5]), .in1(\ınput [7]), .out(\output [6]), .sel(L_R));
  Multiplexer #(.enable("false")) multiplexer_2 (.in0(\ınput [6]), .in1(\ınput [7]), .out(\output [7]), .sel(L_R));
  Multiplexer #(.enable("false")) multiplexer_3 (.in0(\ınput [4]), .in1(\ınput [6]), .out(\output [5]), .sel(L_R));
  Multiplexer #(.enable("false")) multiplexer_4 (.in0(\ınput [3]), .in1(\ınput [5]), .out(\output [4]), .sel(L_R));
  Multiplexer #(.enable("false")) multiplexer_5 (.in0(\ınput [2]), .in1(\ınput [4]), .out(\output [3]), .sel(L_R));
  Multiplexer #(.enable("false")) multiplexer_6 (.in0(\ınput [0]), .in1(\ınput [2]), .out(\output [1]), .sel(L_R));
  Multiplexer #(.enable("false")) multiplexer_7 (.in0(\ınput [1]), .in1(\ınput [3]), .out(\output [2]), .sel(L_R));
  Multiplexer #(.enable("false")) multiplexer_8 (.in0(1'b0), .in1(\ınput [1]), .out(\output [0]), .sel(L_R));
  xor xor_1 (overflow, \output [7], \ınput [7]);
endmodule

module flag_register (
  input  [3:0] ZCNO_in,
  input  CLK,
  output [3:0] ZCNO_out
);

  D_Flip_Flop d_ff_1 (.clk(CLK), .D(ZCNO_in[0]), .Q(ZCNO_out[0]));  // open: Qn, preset, en, reset
  D_Flip_Flop d_ff_2 (.clk(CLK), .D(ZCNO_in[1]), .Q(ZCNO_out[1]));  // open: Qn, preset, en, reset
  D_Flip_Flop d_ff_3 (.clk(CLK), .D(ZCNO_in[2]), .Q(ZCNO_out[2]));  // open: Qn, preset, en, reset
  D_Flip_Flop d_ff_4 (.clk(CLK), .D(ZCNO_in[3]), .Q(ZCNO_out[3]));  // open: Qn, preset, en, reset
endmodule
