// Logisim project control_unit.circ as structural Verilog: 1 circuit, main circuit control unit
module control_unit (
);

  wire ADD, ADDRESSING_MODE, AND, and_1_out, and_2_out, and_3_out, and_4_out, and_5_out, and_6_out,
       and_7_out, and_8_out, and_9_out, and_10_out, and_11_out, and_12_out, and_13_out, and_14_out,
       and_15_out, and_16_out, and_17_out, and_18_out, and_19_out, and_20_out, and_21_out, and_22_out,
       and_23_out, and_24_out, and_25_out, and_26_out, and_27_out, and_28_out, and_29_out, and_30_out,
       and_31_out, and_32_out, and_33_out, and_34_out, and_35_out, and_36_out, and_37_out, and_38_out,
       and_39_out, and_40_out, and_41_out, and_42_out, and_43_out, and_44_out, and_45_out, and_46_out,
       and_47_out, and_48_out, and_49_out, and_50_out, BNE, BRA, C, clr_RAM, DEC, ENABLE, ENABLE_decod, INC,
       L_H, LD, ld_RAM, LSL, LSR, MOV, N, NOT, not_1_out, not_2_out, not_3_out, not_4_out, not_5_out,
       not_6_out, not_7_out, not_8_out, not_11_out, not_14_out, not_15_out, not_16_out, not_17_out,
       not_18_out, not_19_out, not_20_out, not_21_out, not_22_out, not_23_out, not_24_out, not_25_out,
       not_26_out, not_27_out, not_28_out, not_29_out, not_30_out, not_31_out, not_32_out, not_33_out,
       not_34_out, not_35_out, not_36_out, not_37_out, not_38_out, not_39_out, not_40_out, not_41_out,
       not_42_out, not_43_out, not_44_out, not_45_out, not_46_out, not_47_out, not_48_out, not_49_out, O, OR,
       or_1_out, or_2_out, or_3_out, or_4_out, or_5_out, or_6_out, or_7_out, or_8_out, or_9_out, or_10_out,
       PSH, PUL, RESET, sel_RAM, ST, str_RAM, SUB, T0, T1, T2, T3, T4, T5, T6, T7, Z;
  wire [1:0] FunSel_ARF, FunSel_IR, FunSel_RegFile, INC_DEC_FunSel, MuxASel, MuxBSel, not_9_out, not_10_out,
       OutCSel, OutDSel;
  wire [2:0] ARFRegSel, OutASel, OutBSel, RegSel_ARF;
  wire [3:0] ALUFunSel, decoder_1_out0, decoder_2_out0, DESTREG, FunSel_ALU, REGFILE_RegisterSel,
       RegSel_RegFile, Rx, TmpSel;
  wire [7:0] ADDRESS;
  wire [15:12] IR;

  part4_main main_1 (
    .FunSel_RegFile(FunSel_RegFile), .RegSel_RegFile(RegSel_RegFile), .TmpSel(TmpSel), .OutASel(OutASel),
    .OutBSel(OutBSel), .FunSel_ARF(FunSel_ARF), .FunSel_IR(FunSel_IR), .OutCSel(OutCSel), .MuxBSel(MuxBSel),
    .MuxASel(MuxASel), .RegSel_ARF(RegSel_ARF), .OutDSel(OutDSel), .ZCNO({Z, C, N, O}),
    .IR({IR, DESTREG[3], ADDRESSING_MODE, DESTREG[1:0], ADDRESS}), .ENABLE(ENABLE), .FunSel_ALU(FunSel_ALU),
    .str_RAM(str_RAM), .sel_RAM(sel_RAM), .ld_RAM(ld_RAM), .clr_RAM(clr_RAM), .L_H(L_H));
  assign MuxBSel = or_1_out ? 2'b10 : 2'bz;  // Controlled_Buffer controlled_buffer_1
  assign RegSel_ARF = or_1_out ? 3'b011 : 3'bz;  // Controlled_Buffer controlled_buffer_2
  assign FunSel_ARF = or_1_out ? 2'b10 : 2'bz;  // Controlled_Buffer controlled_buffer_3
  assign RESET = or_1_out ? 1'b1 : 1'bz;  // Controlled_Buffer controlled_buffer_4
  and and_1 (and_1_out, BNE, ADDRESSING_MODE, T3, not_3_out);
  and and_2 (and_2_out, ADDRESSING_MODE, T3, BRA);
  or or_1 (or_1_out, and_2_out, and_1_out);
  not not_1 (not_1_out, ADDRESS[6]);
  and and_3 (and_3_out, BNE, ADDRESSING_MODE, T3, Z);
  assign RESET = and_3_out ? 1'b1 : 1'bz;  // Controlled_Buffer controlled_buffer_5
  or or_2 (or_2_out, MOV, NOT, LSR, LSL);
  and and_4 (and_4_out, and_7_out, ADDRESSING_MODE, ADDRESS[6]);
  not not_2 (not_2_out, ADDRESS[6]);
  and and_5 (and_5_out, and_7_out, not_2_out, ADDRESSING_MODE);
  and and_6 (and_6_out, and_8_out, not_1_out, ADDRESSING_MODE);
  assign RegSel_RegFile = and_6_out ? REGFILE_RegisterSel : 4'bz;  // Controlled_Buffer controlled_buffer_6
  assign FunSel_RegFile = and_6_out ? 2'b10 : 2'bz;  // Controlled_Buffer controlled_buffer_7
  assign MuxASel = and_6_out ? 2'b00 : 2'bz;  // Controlled_Buffer controlled_buffer_8
  assign FunSel_ALU = and_6_out ? ALUFunSel : 4'bz;  // Controlled_Buffer controlled_buffer_9
  assign OutASel = and_6_out ? {1'b1, DESTREG[1:0]} : 3'bz;  // Controlled_Buffer controlled_buffer_10
  assign RESET = and_6_out ? 1'b1 : 1'bz;  // Controlled_Buffer controlled_buffer_11
  not not_3 (not_3_out, Z);
  and and_7 (and_7_out, or_2_out, T3);
  assign FunSel_ALU = and_4_out ? ALUFunSel : 4'bz;  // Controlled_Buffer controlled_buffer_12
  assign OutASel = and_4_out ? {1'b0, ADDRESS[5:4]} : 3'bz;  // Controlled_Buffer controlled_buffer_13
  assign RegSel_RegFile = and_4_out ? REGFILE_RegisterSel : 4'bz;  // Controlled_Buffer controlled_buffer_14
  assign FunSel_RegFile = and_4_out ? 2'b10 : 2'bz;  // Controlled_Buffer controlled_buffer_15
  assign TmpSel = and_4_out ? 4'b1111 : 4'bz;  // Controlled_Buffer controlled_buffer_16
  assign MuxASel = and_4_out ? 2'b00 : 2'bz;  // Controlled_Buffer controlled_buffer_17
  assign RESET = and_4_out ? 1'b1 : 1'bz;  // Controlled_Buffer controlled_buffer_18
  assign OutCSel = and_5_out ? ADDRESS[5:4] : 2'bz;  // Controlled_Buffer controlled_buffer_19
  assign TmpSel = and_5_out ? REGFILE_RegisterSel : 4'bz;  // Controlled_Buffer controlled_buffer_20
  assign FunSel_RegFile = and_5_out ? 2'b10 : 2'bz;  // Controlled_Buffer controlled_buffer_21
  assign RegSel_RegFile = and_5_out ? 4'b1111 : 4'bz;  // Controlled_Buffer controlled_buffer_22
  assign MuxASel = and_5_out ? 2'b11 : 2'bz;  // Controlled_Buffer controlled_buffer_23
  assign RESET = and_5_out ? 1'b0 : 1'bz;  // Controlled_Buffer controlled_buffer_24
  or or_3 (or_3_out, MOV, NOT, LSR, LSL);
  and and_8 (and_8_out, or_3_out, T4);
  Hex_Digit_Display hex_digit_display_1 (.value(IR));  // open: dp
  Hex_Digit_Display hex_digit_display_2 (.value({DESTREG[3], ADDRESSING_MODE, DESTREG[1:0]}));  // open: dp
  Multiplexer #(.select(2), .width(3), .enable("false")) multiplexer_1 (
    .in0(3'b011), .in1(3'b011), .in2(3'b101), .in3(3'b110), .out(ARFRegSel), .sel(DESTREG[1:0]));
  Hex_Digit_Display hex_digit_display_3 (.value(ADDRESS[3:0]));  // open: dp
  Hex_Digit_Display hex_digit_display_4 (.value(ADDRESS[7:4]));  // open: dp
  and and_9 (and_9_out, ADDRESSING_MODE, and_13_out);
  not not_4 (not_4_out, ADDRESS[6]);
  and and_10 (and_10_out, and_7_out, not_4_out, not_5_out);
  not not_5 (not_5_out, ADDRESSING_MODE);
  and and_11 (and_11_out, and_7_out, not_6_out, ADDRESS[6]);
  not not_6 (not_6_out, ADDRESSING_MODE);
  not not_7 (not_7_out, ADDRESS[6]);
  and and_12 (and_12_out, and_8_out, not_7_out, not_8_out);
  not not_8 (not_8_out, ADDRESSING_MODE);
  Decoder #(.select(2), .enable("false")) decoder_1 (
    .out0(decoder_1_out0[0]), .out1(decoder_1_out0[1]), .out2(decoder_1_out0[2]), .out3(decoder_1_out0[3]),
    .sel(not_9_out));
  assign not_9_out = ~DESTREG[1:0];  // NOT_Gate not_9, 2 bits wide
  Decoder #(.select(2), .enable("false")) decoder_2 (
    .out0(decoder_2_out0[0]), .out1(decoder_2_out0[1]), .out2(decoder_2_out0[2]), .out3(decoder_2_out0[3]),
    .sel(not_10_out));
  assign not_10_out = ~DESTREG[1:0];  // NOT_Gate not_10, 2 bits wide
  assign MuxASel = and_9_out ? 2'b10 : 2'bz;  // Controlled_Buffer controlled_buffer_25
  assign FunSel_RegFile = and_9_out ? 2'b10 : 2'bz;  // Controlled_Buffer controlled_buffer_26
  assign TmpSel = and_9_out ? 4'b1111 : 4'bz;  // Controlled_Buffer controlled_buffer_27
  assign RegSel_RegFile = and_9_out ? Rx : 4'bz;  // Controlled_Buffer controlled_buffer_28
  assign RESET = and_9_out ? 1'b1 : 1'bz;  // Controlled_Buffer controlled_buffer_29
  assign OutCSel = and_10_out ? ADDRESS[5:4] : 2'bz;  // Controlled_Buffer controlled_buffer_30
  assign TmpSel = and_10_out ? REGFILE_RegisterSel : 4'bz;  // Controlled_Buffer controlled_buffer_31
  assign FunSel_RegFile = and_10_out ? 2'b10 : 2'bz;  // Controlled_Buffer controlled_buffer_32
  assign RegSel_RegFile = and_10_out ? 4'b1111 : 4'bz;  // Controlled_Buffer controlled_buffer_33
  assign MuxASel = and_10_out ? 2'b11 : 2'bz;  // Controlled_Buffer controlled_buffer_34
  assign RESET = and_10_out ? 1'b0 : 1'bz;  // Controlled_Buffer controlled_buffer_35
  assign OutASel = and_11_out ? {1'b0, ADDRESS[5:4]} : 3'bz;  // Controlled_Buffer controlled_buffer_36
  assign FunSel_ALU = and_11_out ? ALUFunSel : 4'bz;  // Controlled_Buffer controlled_buffer_37
  assign MuxBSel = and_11_out ? 2'b00 : 2'bz;  // Controlled_Buffer controlled_buffer_38
  assign RegSel_ARF = and_11_out ? ARFRegSel : 3'bz;  // Controlled_Buffer controlled_buffer_39
  assign FunSel_ARF = and_11_out ? 2'b10 : 2'bz;  // Controlled_Buffer controlled_buffer_40
  assign TmpSel = and_11_out ? 4'b1111 : 4'bz;  // Controlled_Buffer controlled_buffer_41
  assign RegSel_RegFile = and_11_out ? 4'b1111 : 4'bz;  // Controlled_Buffer controlled_buffer_42
  assign RESET = and_11_out ? 1'b1 : 1'bz;  // Controlled_Buffer controlled_buffer_43
  assign RegSel_ARF = and_12_out ? ARFRegSel : 3'bz;  // Controlled_Buffer controlled_buffer_44
  assign FunSel_ARF = and_12_out ? 2'b10 : 2'bz;  // Controlled_Buffer controlled_buffer_45
  assign MuxBSel = and_12_out ? 2'b00 : 2'bz;  // Controlled_Buffer controlled_buffer_46
  assign FunSel_ALU = and_12_out ? ALUFunSel : 4'bz;  // Controlled_Buffer controlled_buffer_47
  assign OutASel = and_12_out ? {1'b1, DESTREG[1:0]} : 3'bz;  // Controlled_Buffer controlled_buffer_48
  assign RESET = and_12_out ? 1'b1 : 1'bz;  // Controlled_Buffer controlled_buffer_49
  decod decod_1 (.RESET(RESET), .T0(T0), .T1(T1), .T2(T2), .T3(T3), .T4(T4), .T5(T5), .T6(T6), .T7(T7));
  and and_13 (and_13_out, LD, T3);
  not not_11 (not_11_out, ADDRESSING_MODE);
  assign Rx = ~decoder_1_out0;  // NOT_Gate not_12, 4 bits wide
  assign REGFILE_RegisterSel = ~decoder_2_out0;  // NOT_Gate not_13, 4 bits wide
  and and_14 (and_14_out, not_11_out, and_13_out);
  assign MuxASel = and_14_out ? 2'b01 : 2'bz;  // Controlled_Buffer controlled_buffer_50
  assign FunSel_RegFile = and_14_out ? 2'b10 : 2'bz;  // Controlled_Buffer controlled_buffer_51
  assign TmpSel = and_14_out ? 4'b1111 : 4'bz;  // Controlled_Buffer controlled_buffer_52
  assign RegSel_RegFile = and_14_out ? Rx : 4'bz;  // Controlled_Buffer controlled_buffer_53
  assign OutDSel = and_14_out ? 2'b10 : 2'bz;  // Controlled_Buffer controlled_buffer_54
  assign RegSel_ARF = and_14_out ? 3'b111 : 3'bz;  // Controlled_Buffer controlled_buffer_55
  assign sel_RAM = and_14_out ? 1'b1 : 1'bz;  // Controlled_Buffer controlled_buffer_56
  assign ld_RAM = and_14_out ? 1'b1 : 1'bz;  // Controlled_Buffer controlled_buffer_57
  assign clr_RAM = and_14_out ? 1'b0 : 1'bz;  // Controlled_Buffer controlled_buffer_58
  assign str_RAM = and_14_out ? 1'b0 : 1'bz;  // Controlled_Buffer controlled_buffer_59
  assign RESET = and_14_out ? 1'b1 : 1'bz;  // Controlled_Buffer controlled_buffer_60
  assign OutDSel = T0 ? 2'b00 : 2'bz;  // Controlled_Buffer controlled_buffer_61
  assign FunSel_ARF = T0 ? 2'b01 : 2'bz;  // Controlled_Buffer controlled_buffer_62
  assign ENABLE = T0 ? 1'b1 : 1'bz;  // Controlled_Buffer controlled_buffer_63
  assign L_H = T0 ? 1'b1 : 1'bz;  // Controlled_Buffer controlled_buffer_64
  assign FunSel_IR = T0 ? 2'b10 : 2'bz;  // Controlled_Buffer controlled_buffer_65
  assign sel_RAM = T0 ? 1'b1 : 1'bz;  // Controlled_Buffer controlled_buffer_66
  assign ld_RAM = T0 ? 1'b1 : 1'bz;  // Controlled_Buffer controlled_buffer_67
  assign clr_RAM = T0 ? 1'b0 : 1'bz;  // Controlled_Buffer controlled_buffer_68
  assign str_RAM = T0 ? 1'b0 : 1'bz;  // Controlled_Buffer controlled_buffer_69
  assign RegSel_ARF = T0 ? 3'b011 : 3'bz;  // Controlled_Buffer controlled_buffer_70
  assign RESET = T0 ? 1'b0 : 1'bz;  // Controlled_Buffer controlled_buffer_71
  or or_4 (or_4_out, INC, DEC);
  or or_5 (or_5_out, INC, DEC);
  or or_6 (or_6_out, INC, DEC);
  Multiplexer #(.select(4), .width(4), .enable("false")) multiplexer_2 (
    .in3(4'b0000), .in4(4'b0111), .in5(4'b1000), .in6(4'b0010), .in7(4'b0100), .in8(4'b0110), .in9(4'b1010),
    .in10(4'b1011), .in13(4'b0000), .in14(4'b0000), .out(ALUFunSel), .sel(IR));  // open: in0, in1, in2, in11, in12, in15
  not not_14 (not_14_out, ADDRESSING_MODE);
  or or_7 (or_7_out, INC, DEC);
  and and_15 (and_15_out, and_24_out, ADDRESSING_MODE, ADDRESS[6]);
  not not_15 (not_15_out, ADDRESS[6]);
  and and_16 (and_16_out, and_24_out, not_15_out, ADDRESSING_MODE);
  and and_17 (and_17_out, or_4_out, T4);
  and and_18 (and_18_out, and_17_out, not_16_out);
  not not_16 (not_16_out, ADDRESSING_MODE);
  and and_19 (and_19_out, or_5_out, T5);
  and and_20 (and_20_out, and_19_out, not_17_out);
  not not_17 (not_17_out, ADDRESSING_MODE);
  and and_21 (and_21_out, or_6_out, T6);
  and and_22 (and_22_out, and_21_out, not_18_out);
  not not_18 (not_18_out, ADDRESSING_MODE);
  assign FunSel_ARF = T1 ? 2'b01 : 2'bz;  // Controlled_Buffer controlled_buffer_72
  assign OutDSel = T1 ? 2'b00 : 2'bz;  // Controlled_Buffer controlled_buffer_73
  assign L_H = T1 ? 1'b0 : 1'bz;  // Controlled_Buffer controlled_buffer_74
  assign FunSel_IR = T1 ? 2'b10 : 2'bz;  // Controlled_Buffer controlled_buffer_75
  assign sel_RAM = T1 ? 1'b1 : 1'bz;  // Controlled_Buffer controlled_buffer_76
  assign ld_RAM = T1 ? 1'b1 : 1'bz;  // Controlled_Buffer controlled_buffer_77
  assign clr_RAM = T1 ? 1'b0 : 1'bz;  // Controlled_Buffer controlled_buffer_78
  assign str_RAM = T1 ? 1'b0 : 1'bz;  // Controlled_Buffer controlled_buffer_79
  assign RegSel_ARF = T1 ? 3'b011 : 3'bz;  // Controlled_Buffer controlled_buffer_80
  assign ENABLE = T1 ? 1'b1 : 1'bz;  // Controlled_Buffer controlled_buffer_81
  assign RESET = T1 ? 1'b0 : 1'bz;  // Controlled_Buffer controlled_buffer_82
  and and_23 (and_23_out, not_14_out, T3, ST);
  and and_24 (and_24_out, or_7_out, T3);
  assign FunSel_ALU = and_15_out ? ALUFunSel : 4'bz;  // Controlled_Buffer controlled_buffer_83
  assign OutASel = and_15_out ? {1'b0, ADDRESS[5:4]} : 3'bz;  // Controlled_Buffer controlled_buffer_84
  assign RegSel_RegFile = and_15_out ? REGFILE_RegisterSel : 4'bz;  // Controlled_Buffer controlled_buffer_85
  assign FunSel_RegFile = and_15_out ? 2'b10 : 2'bz;  // Controlled_Buffer controlled_buffer_86
  assign MuxASel = and_15_out ? 2'b00 : 2'bz;  // Controlled_Buffer controlled_buffer_87
  assign RESET = and_15_out ? 1'b0 : 1'bz;  // Controlled_Buffer controlled_buffer_88
  assign OutCSel = and_16_out ? ADDRESS[5:4] : 2'bz;  // Controlled_Buffer controlled_buffer_89
  assign RegSel_RegFile = and_16_out ? REGFILE_RegisterSel : 4'bz;  // Controlled_Buffer controlled_buffer_90
  assign FunSel_RegFile = and_16_out ? 2'b10 : 2'bz;  // Controlled_Buffer controlled_buffer_91
  assign MuxASel = and_16_out ? 2'b11 : 2'bz;  // Controlled_Buffer controlled_buffer_92
  assign RESET = and_16_out ? 1'b0 : 1'bz;  // Controlled_Buffer controlled_buffer_93
  assign RegSel_ARF = and_18_out ? ARFRegSel : 3'bz;  // Controlled_Buffer controlled_buffer_94
  assign FunSel_ARF = and_18_out ? INC_DEC_FunSel : 2'bz;  // Controlled_Buffer controlled_buffer_95
  assign RESET = and_18_out ? 1'b0 : 1'bz;  // Controlled_Buffer controlled_buffer_96
  assign OutCSel = and_20_out ? DESTREG[1:0] : 2'bz;  // Controlled_Buffer controlled_buffer_97
  assign TmpSel = and_20_out ? REGFILE_RegisterSel : 4'bz;  // Controlled_Buffer controlled_buffer_98
  assign FunSel_RegFile = and_20_out ? 2'b10 : 2'bz;  // Controlled_Buffer controlled_buffer_99
  assign MuxASel = and_20_out ? 2'b11 : 2'bz;  // Controlled_Buffer controlled_buffer_100
  assign RESET = and_20_out ? 1'b0 : 1'bz;  // Controlled_Buffer controlled_buffer_101
  assign RegSel_RegFile = and_20_out ? 4'b1111 : 4'bz;  // Controlled_Buffer controlled_buffer_102
  assign OutASel = and_22_out ? {1'b1, DESTREG[1:0]} : 3'bz;  // Controlled_Buffer controlled_buffer_103
  assign FunSel_ALU = and_22_out ? ALUFunSel : 4'bz;  // Controlled_Buffer controlled_buffer_104
  assign RESET = and_22_out ? 1'b1 : 1'bz;  // Controlled_Buffer controlled_buffer_105
  assign RegSel_RegFile = and_23_out ? 4'b1111 : 4'bz;  // Controlled_Buffer controlled_buffer_106
  assign TmpSel = and_23_out ? 4'b1111 : 4'bz;  // Controlled_Buffer controlled_buffer_107
  assign FunSel_ALU = and_23_out ? 4'b0000 : 4'bz;  // Controlled_Buffer controlled_buffer_108
  assign OutDSel = and_23_out ? 2'b10 : 2'bz;  // Controlled_Buffer controlled_buffer_109
  assign RegSel_ARF = and_23_out ? 3'b111 : 3'bz;  // Controlled_Buffer controlled_buffer_110
  assign sel_RAM = and_23_out ? 1'b1 : 1'bz;  // Controlled_Buffer controlled_buffer_111
  assign ld_RAM = and_23_out ? 1'b0 : 1'bz;  // Controlled_Buffer controlled_buffer_112
  assign clr_RAM = and_23_out ? 1'b0 : 1'bz;  // Controlled_Buffer controlled_buffer_113
  assign str_RAM = and_23_out ? 1'b1 : 1'bz;  // Controlled_Buffer controlled_buffer_114
  assign OutASel = and_23_out ? {1'b0, DESTREG[1:0]} : 3'bz;  // Controlled_Buffer controlled_buffer_115
  assign RESET = and_23_out ? 1'b1 : 1'bz;  // Controlled_Buffer controlled_buffer_116
  Multiplexer #(.width(2), .enable("false")) multiplexer_3 (
    .in0(2'b00), .in1(2'b01), .out(INC_DEC_FunSel), .sel(IR[12]));
  assign ENABLE_decod = T2 ? 1'b1 : 1'bz;  // Controlled_Buffer controlled_buffer_117
  assign ENABLE = T2 ? 1'b0 : 1'bz;  // Controlled_Buffer controlled_buffer_118
  assign RESET = T2 ? 1'b0 : 1'bz;  // Controlled_Buffer controlled_buffer_119
  assign RegSel_RegFile = T2 ? 4'b1111 : 4'bz;  // Controlled_Buffer controlled_buffer_120
  assign TmpSel = T2 ? 4'b1111 : 4'bz;  // Controlled_Buffer controlled_buffer_121
  assign RegSel_ARF = T2 ? 3'b111 : 3'bz;  // Controlled_Buffer controlled_buffer_122
  not not_19 (not_19_out, ADDRESS[6]);
  and and_25 (and_25_out, and_24_out, not_19_out, not_20_out);
  not not_20 (not_20_out, ADDRESSING_MODE);
  not not_21 (not_21_out, ADDRESSING_MODE);
  and and_26 (and_26_out, and_24_out, not_21_out, ADDRESS[6]);
  and and_27 (and_27_out, and_17_out, ADDRESSING_MODE);
  and and_28 (and_28_out, and_19_out, ADDRESSING_MODE);
  assign FunSel_ARF = and_25_out ? 2'b10 : 2'bz;  // Controlled_Buffer controlled_buffer_123
  assign RESET = and_25_out ? 1'b0 : 1'bz;  // Controlled_Buffer controlled_buffer_124
  assign RegSel_ARF = and_25_out ? ARFRegSel : 3'bz;  // Controlled_Buffer controlled_buffer_125
  assign OutCSel = and_25_out ? ADDRESS[5:4] : 2'bz;  // Controlled_Buffer controlled_buffer_126
  assign MuxBSel = and_25_out ? 2'b11 : 2'bz;  // Controlled_Buffer controlled_buffer_127
  assign OutASel = and_26_out ? {1'b0, ADDRESS[5:4]} : 3'bz;  // Controlled_Buffer controlled_buffer_128
  assign FunSel_ALU = and_26_out ? ALUFunSel : 4'bz;  // Controlled_Buffer controlled_buffer_129
  assign MuxBSel = and_26_out ? 2'b00 : 2'bz;  // Controlled_Buffer controlled_buffer_130
  assign RegSel_ARF = and_26_out ? ARFRegSel : 3'bz;  // Controlled_Buffer controlled_buffer_131
  assign FunSel_ARF = and_26_out ? 2'b10 : 2'bz;  // Controlled_Buffer controlled_buffer_132
  assign RESET = and_26_out ? 1'b0 : 1'bz;  // Controlled_Buffer controlled_buffer_133
  assign FunSel_RegFile = and_27_out ? INC_DEC_FunSel : 2'bz;  // Controlled_Buffer controlled_buffer_134
  assign RESET = and_27_out ? 1'b0 : 1'bz;  // Controlled_Buffer controlled_buffer_135
  assign RegSel_RegFile = and_27_out ? REGFILE_RegisterSel : 4'bz;  // Controlled_Buffer controlled_buffer_136
  assign OutASel = and_28_out ? {1'b0, DESTREG[1:0]} : 3'bz;  // Controlled_Buffer controlled_buffer_137
  assign FunSel_ALU = and_28_out ? ALUFunSel : 4'bz;  // Controlled_Buffer controlled_buffer_138
  assign RESET = and_28_out ? 1'b1 : 1'bz;  // Controlled_Buffer controlled_buffer_139
  and and_29 (and_29_out, PSH, T3);
  Decoder #(.select(4)) decoder_3 (
    .out0(BRA), .out1(LD), .out2(ST), .out3(MOV), .out4(AND), .out5(OR), .out6(NOT), .out7(ADD), .out8(SUB),
    .out9(LSR), .out10(LSL), .out11(PUL), .out12(PSH), .out13(INC), .out14(DEC), .out15(BNE), .sel(IR),
    .en(ENABLE_decod));
  assign OutDSel = and_29_out ? 2'b11 : 2'bz;  // Controlled_Buffer controlled_buffer_140
  assign RegSel_ARF = and_29_out ? 3'b110 : 3'bz;  // Controlled_Buffer controlled_buffer_141
  assign sel_RAM = and_29_out ? 1'b1 : 1'bz;  // Controlled_Buffer controlled_buffer_142
  assign ld_RAM = and_29_out ? 1'b0 : 1'bz;  // Controlled_Buffer controlled_buffer_143
  assign clr_RAM = and_29_out ? 1'b0 : 1'bz;  // Controlled_Buffer controlled_buffer_144
  assign str_RAM = and_29_out ? 1'b1 : 1'bz;  // Controlled_Buffer controlled_buffer_145
  assign OutASel = and_29_out ? {1'b0, DESTREG[1:0]} : 3'bz;  // Controlled_Buffer controlled_buffer_146
  assign FunSel_ARF = and_29_out ? 2'b00 : 2'bz;  // Controlled_Buffer controlled_buffer_147
  assign FunSel_ALU = and_29_out ? 4'b0000 : 4'bz;  // Controlled_Buffer controlled_buffer_148
  assign RegSel_RegFile = and_29_out ? 4'b1111 : 4'bz;  // Controlled_Buffer controlled_buffer_149
  assign TmpSel = and_29_out ? 4'b1111 : 4'bz;  // Controlled_Buffer controlled_buffer_150
  assign RESET = and_29_out ? 1'b1 : 1'bz;  // Controlled_Buffer controlled_buffer_151
  or or_8 (or_8_out, AND, OR, ADD, SUB);
  and and_30 (and_30_out, PUL, T3);
  assign RegSel_ARF = and_30_out ? 3'b110 : 3'bz;  // Controlled_Buffer controlled_buffer_152
  assign FunSel_ARF = and_30_out ? 2'b01 : 2'bz;  // Controlled_Buffer controlled_buffer_153
  assign RegSel_RegFile = and_30_out ? 4'b1111 : 4'bz;  // Controlled_Buffer controlled_buffer_154
  assign TmpSel = and_30_out ? 4'b1111 : 4'bz;  // Controlled_Buffer controlled_buffer_155
  assign RESET = and_30_out ? 1'b0 : 1'bz;  // Controlled_Buffer controlled_buffer_156
  or or_9 (or_9_out, AND, OR, ADD, SUB);
  and and_31 (and_31_out, or_9_out, T3);
  not not_22 (not_22_out, ADDRESS[6]);
  not not_23 (not_23_out, ADDRESS[2]);
  not not_24 (not_24_out, ADDRESSING_MODE);
  and and_32 (and_32_out, or_8_out, T4);
  not not_25 (not_25_out, ADDRESS[6]);
  not not_26 (not_26_out, ADDRESS[2]);
  not not_27 (not_27_out, ADDRESS[2]);
  not not_28 (not_28_out, ADDRESS[2]);
  not not_29 (not_29_out, ADDRESSING_MODE);
  or or_10 (or_10_out, AND, OR, ADD, SUB);
  and and_33 (and_33_out, or_10_out, T5);
  not not_30 (not_30_out, ADDRESS[6]);
  not not_31 (not_31_out, ADDRESS[2]);
  and and_34 (and_34_out, and_31_out, ADDRESS[6], ADDRESSING_MODE, ADDRESS[2]);
  and and_35 (and_35_out, and_31_out, not_22_out, ADDRESSING_MODE, ADDRESS[2]);
  and and_36 (and_36_out, and_31_out, ADDRESS[6], not_32_out, ADDRESS[2]);
  not not_32 (not_32_out, ADDRESSING_MODE);
  and and_37 (and_37_out, and_31_out, not_23_out, not_24_out, ADDRESS[6]);
  and and_38 (and_38_out, and_32_out, not_25_out, ADDRESSING_MODE, not_26_out);
  and and_39 (and_39_out, and_32_out, not_27_out, ADDRESSING_MODE, ADDRESS[6]);
  and and_40 (and_40_out, and_32_out, not_28_out, not_29_out, ADDRESS[6]);
  and and_41 (and_41_out, and_33_out, not_30_out, ADDRESSING_MODE, not_31_out);
  assign OutBSel = and_34_out ? {1'b0, ADDRESS[5:4]} : 3'bz;  // Controlled_Buffer controlled_buffer_157
  assign OutASel = and_34_out ? {1'b0, ADDRESS[1:0]} : 3'bz;  // Controlled_Buffer controlled_buffer_158
  assign FunSel_ALU = and_34_out ? ALUFunSel : 4'bz;  // Controlled_Buffer controlled_buffer_159
  assign MuxASel = and_34_out ? 2'b00 : 2'bz;  // Controlled_Buffer controlled_buffer_160
  assign FunSel_RegFile = and_34_out ? 2'b10 : 2'bz;  // Controlled_Buffer controlled_buffer_161
  assign RegSel_RegFile = and_34_out ? REGFILE_RegisterSel : 4'bz;  // Controlled_Buffer controlled_buffer_162
  assign RESET = and_34_out ? 1'b1 : 1'bz;  // Controlled_Buffer controlled_buffer_163
  assign OutCSel = and_35_out ? ADDRESS[5:4] : 2'bz;  // Controlled_Buffer controlled_buffer_164
  assign MuxASel = and_35_out ? 2'b11 : 2'bz;  // Controlled_Buffer controlled_buffer_165
  assign FunSel_RegFile = and_35_out ? 2'b10 : 2'bz;  // Controlled_Buffer controlled_buffer_166
  assign TmpSel = and_35_out ? 4'b0111 : 4'bz;  // Controlled_Buffer controlled_buffer_167
  assign RESET = and_35_out ? 1'b0 : 1'bz;  // Controlled_Buffer controlled_buffer_168
  assign RegSel_RegFile = and_35_out ? 4'b1111 : 4'bz;  // Controlled_Buffer controlled_buffer_169
  assign OutBSel = and_36_out ? {1'b0, ADDRESS[5:4]} : 3'bz;  // Controlled_Buffer controlled_buffer_170
  assign OutASel = and_36_out ? {1'b0, ADDRESS[1:0]} : 3'bz;  // Controlled_Buffer controlled_buffer_171
  assign FunSel_ALU = and_36_out ? ALUFunSel : 4'bz;  // Controlled_Buffer controlled_buffer_172
  assign MuxBSel = and_36_out ? 2'b00 : 2'bz;  // Controlled_Buffer controlled_buffer_173
  assign FunSel_ARF = and_36_out ? 2'b10 : 2'bz;  // Controlled_Buffer controlled_buffer_174
  assign RegSel_ARF = and_36_out ? ARFRegSel : 3'bz;  // Controlled_Buffer controlled_buffer_175
  assign RESET = and_36_out ? 1'b1 : 1'bz;  // Controlled_Buffer controlled_buffer_176
  assign OutCSel = and_37_out ? ADDRESS[1:0] : 2'bz;  // Controlled_Buffer controlled_buffer_177
  assign MuxASel = and_37_out ? 2'b11 : 2'bz;  // Controlled_Buffer controlled_buffer_178
  assign FunSel_RegFile = and_37_out ? 2'b10 : 2'bz;  // Controlled_Buffer controlled_buffer_179
  assign TmpSel = and_37_out ? 4'b0111 : 4'bz;  // Controlled_Buffer controlled_buffer_180
  assign RESET = and_37_out ? 1'b0 : 1'bz;  // Controlled_Buffer controlled_buffer_181
  assign RegSel_RegFile = and_37_out ? 4'b1111 : 4'bz;  // Controlled_Buffer controlled_buffer_182
  assign OutCSel = and_38_out ? ADDRESS[5:4] : 2'bz;  // Controlled_Buffer controlled_buffer_183
  assign MuxASel = and_38_out ? 2'b11 : 2'bz;  // Controlled_Buffer controlled_buffer_184
  assign FunSel_RegFile = and_38_out ? 2'b10 : 2'bz;  // Controlled_Buffer controlled_buffer_185
  assign TmpSel = and_38_out ? 4'b1011 : 4'bz;  // Controlled_Buffer controlled_buffer_186
  assign RESET = and_38_out ? 1'b0 : 1'bz;  // Controlled_Buffer controlled_buffer_187
  assign RegSel_RegFile = and_38_out ? 4'b1111 : 4'bz;  // Controlled_Buffer controlled_buffer_188
  assign OutASel = and_39_out ? 3'b100 : 3'bz;  // Controlled_Buffer controlled_buffer_189
  assign OutBSel = and_39_out ? {1'b0, ADDRESS[5:4]} : 3'bz;  // Controlled_Buffer controlled_buffer_190
  assign FunSel_ALU = and_39_out ? ALUFunSel : 4'bz;  // Controlled_Buffer controlled_buffer_191
  assign MuxASel = and_39_out ? 2'b00 : 2'bz;  // Controlled_Buffer controlled_buffer_192
  assign FunSel_RegFile = and_39_out ? 2'b10 : 2'bz;  // Controlled_Buffer controlled_buffer_193
  assign RegSel_RegFile = and_39_out ? REGFILE_RegisterSel : 4'bz;  // Controlled_Buffer controlled_buffer_194
  assign RESET = and_39_out ? 1'b1 : 1'bz;  // Controlled_Buffer controlled_buffer_195
  assign OutASel = and_40_out ? 3'b100 : 3'bz;  // Controlled_Buffer controlled_buffer_196
  assign OutBSel = and_40_out ? {1'b0, ADDRESS[5:4]} : 3'bz;  // Controlled_Buffer controlled_buffer_197
  assign FunSel_ALU = and_40_out ? ALUFunSel : 4'bz;  // Controlled_Buffer controlled_buffer_198
  assign MuxBSel = and_40_out ? 2'b00 : 2'bz;  // Controlled_Buffer controlled_buffer_199
  assign FunSel_ARF = and_40_out ? 2'b10 : 2'bz;  // Controlled_Buffer controlled_buffer_200
  assign RegSel_ARF = and_40_out ? ARFRegSel : 3'bz;  // Controlled_Buffer controlled_buffer_201
  assign RESET = and_40_out ? 1'b1 : 1'bz;  // Controlled_Buffer controlled_buffer_202
  assign OutASel = and_41_out ? 3'b100 : 3'bz;  // Controlled_Buffer controlled_buffer_203
  assign OutBSel = and_41_out ? 3'b101 : 3'bz;  // Controlled_Buffer controlled_buffer_204
  assign FunSel_ALU = and_41_out ? ALUFunSel : 4'bz;  // Controlled_Buffer controlled_buffer_205
  assign MuxASel = and_41_out ? 2'b00 : 2'bz;  // Controlled_Buffer controlled_buffer_206
  assign FunSel_RegFile = and_41_out ? 2'b10 : 2'bz;  // Controlled_Buffer controlled_buffer_207
  assign RegSel_RegFile = and_41_out ? REGFILE_RegisterSel : 4'bz;  // Controlled_Buffer controlled_buffer_208
  assign RESET = and_41_out ? 1'b1 : 1'bz;  // Controlled_Buffer controlled_buffer_209
  and and_42 (and_42_out, PUL, T4);
  assign OutDSel = and_42_out ? 2'b11 : 2'bz;  // Controlled_Buffer controlled_buffer_210
  assign RegSel_ARF = and_42_out ? 3'b111 : 3'bz;  // Controlled_Buffer controlled_buffer_211
  assign sel_RAM = and_42_out ? 1'b1 : 1'bz;  // Controlled_Buffer controlled_buffer_212
  assign ld_RAM = and_42_out ? 1'b1 : 1'bz;  // Controlled_Buffer controlled_buffer_213
  assign clr_RAM = and_42_out ? 1'b0 : 1'bz;  // Controlled_Buffer controlled_buffer_214
  assign str_RAM = and_42_out ? 1'b0 : 1'bz;  // Controlled_Buffer controlled_buffer_215
  assign RegSel_RegFile = and_42_out ? Rx : 4'bz;  // Controlled_Buffer controlled_buffer_216
  assign TmpSel = and_42_out ? 4'b1111 : 4'bz;  // Controlled_Buffer controlled_buffer_217
  assign MuxASel = and_42_out ? 2'b01 : 2'bz;  // Controlled_Buffer controlled_buffer_218
  assign FunSel_RegFile = and_42_out ? 2'b10 : 2'bz;  // Controlled_Buffer controlled_buffer_219
  assign RESET = and_42_out ? 1'b1 : 1'bz;  // Controlled_Buffer controlled_buffer_220
  not not_33 (not_33_out, ADDRESS[2]);
  not not_34 (not_34_out, ADDRESS[6]);
  not not_35 (not_35_out, ADDRESS[2]);
  not not_36 (not_36_out, ADDRESS[2]);
  and and_43 (and_43_out, and_31_out, not_36_out, ADDRESSING_MODE, ADDRESS[6]);
  not not_37 (not_37_out, ADDRESS[6]);
  and and_44 (and_44_out, and_31_out, not_37_out, not_38_out, not_33_out);
  not not_38 (not_38_out, ADDRESSING_MODE);
  not not_39 (not_39_out, ADDRESS[6]);
  and and_45 (and_45_out, and_31_out, not_39_out, not_40_out, ADDRESS[2]);
  not not_40 (not_40_out, ADDRESSING_MODE);
  and and_46 (and_46_out, and_31_out, not_34_out, ADDRESSING_MODE, not_35_out);
  assign OutCSel = and_46_out ? ADDRESS[1:0] : 2'bz;  // Controlled_Buffer controlled_buffer_221
  assign MuxASel = and_46_out ? 2'b11 : 2'bz;  // Controlled_Buffer controlled_buffer_222
  assign FunSel_RegFile = and_46_out ? 2'b10 : 2'bz;  // Controlled_Buffer controlled_buffer_223
  assign TmpSel = and_46_out ? 4'b0111 : 4'bz;  // Controlled_Buffer controlled_buffer_224
  assign RESET = and_46_out ? 1'b0 : 1'bz;  // Controlled_Buffer controlled_buffer_225
  assign RegSel_RegFile = and_46_out ? 4'b1111 : 4'bz;  // Controlled_Buffer controlled_buffer_226
  assign OutCSel = and_43_out ? ADDRESS[1:0] : 2'bz;  // Controlled_Buffer controlled_buffer_227
  assign MuxASel = and_43_out ? 2'b11 : 2'bz;  // Controlled_Buffer controlled_buffer_228
  assign FunSel_RegFile = and_43_out ? 2'b10 : 2'bz;  // Controlled_Buffer controlled_buffer_229
  assign TmpSel = and_43_out ? 4'b0111 : 4'bz;  // Controlled_Buffer controlled_buffer_230
  assign RESET = and_43_out ? 1'b0 : 1'bz;  // Controlled_Buffer controlled_buffer_231
  assign RegSel_RegFile = and_43_out ? 4'b1111 : 4'bz;  // Controlled_Buffer controlled_buffer_232
  assign OutCSel = and_44_out ? ADDRESS[1:0] : 2'bz;  // Controlled_Buffer controlled_buffer_233
  assign MuxASel = and_44_out ? 2'b11 : 2'bz;  // Controlled_Buffer controlled_buffer_234
  assign FunSel_RegFile = and_44_out ? 2'b10 : 2'bz;  // Controlled_Buffer controlled_buffer_235
  assign TmpSel = and_44_out ? 4'b0111 : 4'bz;  // Controlled_Buffer controlled_buffer_236
  assign RESET = and_44_out ? 1'b0 : 1'bz;  // Controlled_Buffer controlled_buffer_237
  assign RegSel_RegFile = and_44_out ? 4'b1111 : 4'bz;  // Controlled_Buffer controlled_buffer_238
  assign OutCSel = and_45_out ? ADDRESS[5:4] : 2'bz;  // Controlled_Buffer controlled_buffer_239
  assign MuxASel = and_45_out ? 2'b11 : 2'bz;  // Controlled_Buffer controlled_buffer_240
  assign FunSel_RegFile = and_45_out ? 2'b10 : 2'bz;  // Controlled_Buffer controlled_buffer_241
  assign TmpSel = and_45_out ? 4'b0111 : 4'bz;  // Controlled_Buffer controlled_buffer_242
  assign RESET = and_45_out ? 1'b0 : 1'bz;  // Controlled_Buffer controlled_buffer_243
  assign RegSel_RegFile = and_45_out ? 4'b1111 : 4'bz;  // Controlled_Buffer controlled_buffer_244
  not not_41 (not_41_out, ADDRESS[6]);
  not not_42 (not_42_out, ADDRESS[6]);
  not not_43 (not_43_out, ADDRESSING_MODE);
  not not_44 (not_44_out, ADDRESS[2]);
  not not_45 (not_45_out, ADDRESS[6]);
  and and_47 (and_47_out, and_32_out, not_45_out, not_46_out, ADDRESS[2]);
  not not_46 (not_46_out, ADDRESSING_MODE);
  not not_47 (not_47_out, ADDRESS[6]);
  not not_48 (not_48_out, ADDRESSING_MODE);
  not not_49 (not_49_out, ADDRESS[2]);
  and and_48 (and_48_out, and_32_out, not_41_out, ADDRESSING_MODE, ADDRESS[2]);
  assign OutBSel = and_48_out ? 3'b100 : 3'bz;  // Controlled_Buffer controlled_buffer_245
  assign OutASel = and_48_out ? {1'b0, ADDRESS[1:0]} : 3'bz;  // Controlled_Buffer controlled_buffer_246
  assign FunSel_ALU = and_48_out ? ALUFunSel : 4'bz;  // Controlled_Buffer controlled_buffer_247
  assign MuxASel = and_48_out ? 2'b00 : 2'bz;  // Controlled_Buffer controlled_buffer_248
  assign FunSel_RegFile = and_48_out ? 2'b10 : 2'bz;  // Controlled_Buffer controlled_buffer_249
  assign RegSel_RegFile = and_48_out ? REGFILE_RegisterSel : 4'bz;  // Controlled_Buffer controlled_buffer_250
  assign RESET = and_48_out ? 1'b1 : 1'bz;  // Controlled_Buffer controlled_buffer_251
  and and_49 (and_49_out, and_32_out, not_42_out, not_43_out, not_44_out);
  assign OutBSel = and_47_out ? 3'b100 : 3'bz;  // Controlled_Buffer controlled_buffer_252
  assign OutASel = and_47_out ? {1'b0, ADDRESS[1:0]} : 3'bz;  // Controlled_Buffer controlled_buffer_253
  assign FunSel_ALU = and_47_out ? ALUFunSel : 4'bz;  // Controlled_Buffer controlled_buffer_254
  assign MuxBSel = and_47_out ? 2'b00 : 2'bz;  // Controlled_Buffer controlled_buffer_255
  assign FunSel_ARF = and_47_out ? 2'b10 : 2'bz;  // Controlled_Buffer controlled_buffer_256
  assign RegSel_ARF = and_47_out ? ARFRegSel : 3'bz;  // Controlled_Buffer controlled_buffer_257
  assign RESET = and_47_out ? 1'b1 : 1'bz;  // Controlled_Buffer controlled_buffer_258
  and and_50 (and_50_out, and_33_out, not_47_out, not_48_out, not_49_out);
  assign OutCSel = and_49_out ? ADDRESS[5:4] : 2'bz;  // Controlled_Buffer controlled_buffer_259
  assign MuxASel = and_49_out ? 2'b11 : 2'bz;  // Controlled_Buffer controlled_buffer_260
  assign FunSel_RegFile = and_49_out ? 2'b10 : 2'bz;  // Controlled_Buffer controlled_buffer_261
  assign TmpSel = and_49_out ? 4'b1011 : 4'bz;  // Controlled_Buffer controlled_buffer_262
  assign RESET = and_49_out ? 1'b0 : 1'bz;  // Controlled_Buffer controlled_buffer_263
  assign RegSel_RegFile = and_49_out ? 4'b1111 : 4'bz;  // Controlled_Buffer controlled_buffer_264
  assign OutASel = and_50_out ? 3'b100 : 3'bz;  // Controlled_Buffer controlled_buffer_265
  assign OutBSel = and_50_out ? 3'b101 : 3'bz;  // Controlled_Buffer controlled_buffer_266
  assign FunSel_ALU = and_50_out ? ALUFunSel : 4'bz;  // Controlled_Buffer controlled_buffer_267
  assign MuxBSel = and_50_out ? 2'b00 : 2'bz;  // Controlled_Buffer controlled_buffer_268
  assign FunSel_ARF = and_50_out ? 2'b10 : 2'bz;  // Controlled_Buffer controlled_buffer_269
  assign RegSel_ARF = and_50_out ? ARFRegSel : 3'bz;  // Controlled_Buffer controlled_buffer_270
  assign RESET = and_50_out ? 1'b1 : 1'bz;  // Controlled_Buffer controlled_buffer_271

  // Other names for the same wires on the sheet: IR[11:0] = {DESTREG[3], ADDRESSING_MODE, DESTREG[1:0], ADDRESS};
  //   REGSEL[1:0] = DESTREG[1:0]; SRCREG1[3:0] = ADDRESS[7:4]; SRCREG2[3:0] = ADDRESS[3:0];
  //   DESTREG[2] = ADDRESSING_MODE; OPCODE[3:0] = IR; ZCNO[3:0] = {Z, C, N, O}

  // Notes on the sheet:
  //   PART4
  //   BRA 0X00
  //   BNE 0X0F
  //   RF <- RF
  //   MOV 0X03
  //   NOT 0X06
  //   LSL 0X09
  //   LSR 0X0A
  //   RF <- ARF
  //   RF <- ARF
  //   ARF <- ARF
  //   ARF <- RF
  //   ARF <- ARF
  //   SEQUENTIAL COUNTER
  //   LD 0X01
  //   FETCH CYCLE
  //   RF <- RF
  //   ARF <- ARF
  //   ARF <- RF
  //   ARF <- ARF
  //   ARF <- RF
  //   ST 0X02
  //   INC 0X0D
  //   DEC 0X0E
  //   RF <- ARF
  //   ARF <- ARF
  //   ARF <- RF
  //   RF <- RF
  //   RF <- ARF
  //   RF <- RF
  //   RF <- ARF
  //   DECODE
  //   ARF <- ARF
  //   ARF <- RF
  //   PSH 0X0C
  //   SP <- SP+1
  //   ARF <- RF RF
  //   RF <- RF ARF
  //   ARF <- RF ARF
  //   RF <- ARF ARF
  //   PUL 0X0B
  //   RF <- RF RF
  //   RF <- ARF RF
  //   ARF <- RF ARF
  //   RF <- ARF ARF
  //   Rx <- M[SP]
  //   AND 0X04
  //   OR 0X05
  //   ADD 0X07
  //   SUB 0X08
  //   RF <- ARF ARF
  //   RF <- RF ARF
  //   ARF <- ARF ARF
  //   ARF <- ARF RF
  //   RF <- ARF RF
  //   ARF <- ARF RF
  //   ARF <- ARF ARF
  //   ARF <- ARF ARF
endmodule
