// Logisim project seq_counter.circ as structural Verilog: 3 circuits, main circuit 8-bit_register(part1a)
module _8_bit_register_part1a (
  input  CLK,
  input  ENABLE,
  input  [7:0] INPUT,
  input  [1:0] FUNSEL,
  output [7:0] OUTPUT
);

  wire [7:0] adder_1_out, multiplexer_1_out, subtractor_1_out;

  Hex_Digit_Display hex_digit_display_1 (.value(INPUT[7:4]));  // open: dp
  Hex_Digit_Display hex_digit_display_2 (.value(INPUT[3:0]));  // open: dp
  Subtractor subtractor_1 (.a(OUTPUT), .b(8'h1), .out(subtractor_1_out));  // open: bin, bout
  Adder adder_1 (.a(OUTPUT), .b(8'h1), .out(adder_1_out));  // open: cin, cout
  Multiplexer #(.select(2), .width(8)) multiplexer_1 (
    .in0(subtractor_1_out), .in1(adder_1_out), .in2(INPUT), .in3({8{1'b0}}), .out(multiplexer_1_out),
    .sel(FUNSEL));  // open: en
  D_Flip_Flop d_ff_1 (.clk(CLK), .D(multiplexer_1_out[0]), .Q(OUTPUT[0]), .en(ENABLE));  // open: Qn, preset, reset
  D_Flip_Flop d_ff_2 (.clk(CLK), .D(multiplexer_1_out[1]), .Q(OUTPUT[1]), .en(ENABLE));  // open: Qn, preset, reset
  D_Flip_Flop d_ff_3 (.clk(CLK), .D(multiplexer_1_out[2]), .Q(OUTPUT[2]), .en(ENABLE));  // open: Qn, preset, reset
  D_Flip_Flop d_ff_4 (.clk(CLK), .D(multiplexer_1_out[3]), .Q(OUTPUT[3]), .en(ENABLE));  // open: Qn, preset, reset
  D_Flip_Flop d_ff_5 (.clk(CLK), .D(multiplexer_1_out[4]), .Q(OUTPUT[4]), .en(ENABLE));  // open: Qn, preset, reset
  D_Flip_Flop d_ff_6 (.clk(CLK), .D(multiplexer_1_out[5]), .Q(OUTPUT[5]), .en(ENABLE));  // open: Qn, preset, reset
  D_Flip_Flop d_ff_7 (.clk(CLK), .D(multiplexer_1_out[6]), .Q(OUTPUT[6]), .en(ENABLE));  // open: Qn, preset, reset
  D_Flip_Flop d_ff_8 (.clk(CLK), .D(multiplexer_1_out[7]), .Q(OUTPUT[7]), .en(ENABLE));  // open: Qn, preset, reset
  Hex_Digit_Display hex_digit_display_3 (.value(OUTPUT[7:4]));  // open: dp
  Hex_Digit_Display hex_digit_display_4 (.value(OUTPUT[3:0]));  // open: dp

  // Notes on the sheet:
  //   CLEAR
endmodule

module _16_bit_register_part1b (
  input  ENABLE,
  input  L_H,
  input  [1:0] FunSel,
  input  [7:0] INPUT,
  output [15:0] OUTPUT
);

  wire CLK_out;
  wire [7:0] undriven;
  wire [15:0] adder_1_out, multiplexer_1_out, multiplexer_2_out, subtractor_1_out;
  wire [15:8] undriven_2;

  Hex_Digit_Display hex_digit_display_1 (.value(INPUT[7:4]));  // open: dp
  Hex_Digit_Display hex_digit_display_2 (.value(INPUT[3:0]));  // open: dp
  Multiplexer #(.width(16)) multiplexer_1 (
    .in0({INPUT, undriven}), .in1({undriven_2, INPUT}), .out(multiplexer_1_out), .sel(L_H));  // open: en
  Subtractor #(.width(16)) subtractor_1 (.a(OUTPUT), .b(16'h1), .out(subtractor_1_out));  // open: bin, bout
  Adder #(.width(16)) adder_1 (.a(OUTPUT), .b(16'h1), .out(adder_1_out));  // open: cin, cout
  Multiplexer #(.select(2), .width(16)) multiplexer_2 (
    .in0(subtractor_1_out), .in1(adder_1_out), .in2(multiplexer_1_out), .in3({16{1'b0}}),
    .out(multiplexer_2_out), .sel(FunSel));  // open: en
  Clock CLK (.out(CLK_out));
  D_Flip_Flop d_ff_1 (.clk(CLK_out), .D(multiplexer_2_out[0]), .Q(OUTPUT[0]), .en(ENABLE));  // open: Qn, preset, reset
  D_Flip_Flop d_ff_2 (.clk(CLK_out), .D(multiplexer_2_out[1]), .Q(OUTPUT[1]), .en(ENABLE));  // open: Qn, preset, reset
  D_Flip_Flop d_ff_3 (.clk(CLK_out), .D(multiplexer_2_out[2]), .Q(OUTPUT[2]), .en(ENABLE));  // open: Qn, preset, reset
  D_Flip_Flop d_ff_4 (.clk(CLK_out), .D(multiplexer_2_out[3]), .Q(OUTPUT[3]), .en(ENABLE));  // open: Qn, preset, reset
  D_Flip_Flop d_ff_5 (.clk(CLK_out), .D(multiplexer_2_out[4]), .Q(OUTPUT[4]), .en(ENABLE));  // open: Qn, preset, reset
  D_Flip_Flop d_ff_6 (.clk(CLK_out), .D(multiplexer_2_out[5]), .Q(OUTPUT[5]), .en(ENABLE));  // open: Qn, preset, reset
  D_Flip_Flop d_ff_7 (.clk(CLK_out), .D(multiplexer_2_out[6]), .Q(OUTPUT[6]), .en(ENABLE));  // open: Qn, preset, reset
  D_Flip_Flop d_ff_8 (.clk(CLK_out), .D(multiplexer_2_out[7]), .Q(OUTPUT[7]), .en(ENABLE));  // open: Qn, preset, reset
  D_Flip_Flop d_ff_9 (.clk(CLK_out), .D(multiplexer_2_out[8]), .Q(OUTPUT[8]), .en(ENABLE));  // open: Qn, preset, reset
  D_Flip_Flop d_ff_10 (.clk(CLK_out), .D(multiplexer_2_out[9]), .Q(OUTPUT[9]), .en(ENABLE));  // open: Qn, preset, reset
  D_Flip_Flop d_ff_11 (
    .clk(CLK_out), .D(multiplexer_2_out[10]), .Q(OUTPUT[10]), .en(ENABLE));  // open: Qn, preset, reset
  D_Flip_Flop d_ff_12 (
    .clk(CLK_out), .D(multiplexer_2_out[11]), .Q(OUTPUT[11]), .en(ENABLE));  // open: Qn, preset, reset
  D_Flip_Flop d_ff_13 (
    .clk(CLK_out), .D(multiplexer_2_out[12]), .Q(OUTPUT[12]), .en(ENABLE));  // open: Qn, preset, reset
  D_Flip_Flop d_ff_14 (
    .clk(CLK_out), .D(multiplexer_2_out[13]), .Q(OUTPUT[13]), .en(ENABLE));  // open: Qn, preset, reset
  D_Flip_Flop d_ff_15 (
    .clk(CLK_out), .D(multiplexer_2_out[14]), .Q(OUTPUT[14]), .en(ENABLE));  // open: Qn, preset, reset
  D_Flip_Flop d_ff_16 (
    .clk(CLK_out), .D(multiplexer_2_out[15]), .Q(OUTPUT[15]), .en(ENABLE));  // open: Qn, preset, reset
  Hex_Digit_Display hex_digit_display_3 (.value(OUTPUT[15:12]));  // open: dp
  Hex_Digit_Display hex_digit_display_4 (.value(OUTPUT[7:4]));  // open: dp
  Hex_Digit_Display hex_digit_display_5 (.value(OUTPUT[11:8]));  // open: dp
  Hex_Digit_Display hex_digit_display_6 (.value(OUTPUT[3:0]));  // open: dp

  // Notes on the sheet:
  //   CLEAR
endmodule

module decod (
  input  RESET,
  output T0,
  output T1,
  output T2,
  output T3,
  output T4,
  output T5,
  output T6,
  output T7
);

  wire clock_1_out;
  wire [1:0] multiplexer_1_out;
  wire [7:0] n8_bit_register_part1a_1_output;

  Clock clock_1 (.out(clock_1_out));
  Multiplexer #(.width(2), .enable("false")) multiplexer_1 (
    .in0(2'b01), .in1(2'b11), .out(multiplexer_1_out), .sel(RESET));
  _8_bit_register_part1a u_8_bit_register_part1a_1 (
    .OUTPUT(n8_bit_register_part1a_1_output), .CLK(clock_1_out), .ENABLE(1'b1), .FUNSEL(multiplexer_1_out));  // open: INPUT
  Decoder #(.select(3), .enable("false")) decoder_1 (
    .out0(T0), .out1(T1), .out2(T2), .out3(T3), .out4(T4), .out5(T5), .out6(T6), .out7(T7),
    .sel(n8_bit_register_part1a_1_output[2:0]));
endmodule
